// Logisim project ALU.circ as structural Verilog: 5 circuits, main circuit main
module main (
  input  [1:0] OP,
  input  Bnegate,
  input  in_3,
  input  in_4,
  input  in_5,
  input  in_6,
  input  in_7,
  input  in_8,
  input  in_9,
  input  in_10,
  input  in_11,
  input  in_12,
  input  in_13,
  input  in_14,
  input  in_15,
  input  in_16,
  input  in_17,
  input  in_18,
  input  in_19,
  input  in_20,
  input  in_21,
  input  in_22,
  input  in_23,
  input  in_24,
  input  in_25,
  input  in_26,
  input  in_27,
  input  in_28,
  input  in_29,
  input  in_30,
  input  in_31,
  input  in_32,
  input  in_33,
  input  in_34,
  input  in_35,
  input  in_36,
  input  in_37,
  input  in_38,
  input  in_39,
  input  in_40,
  input  in_41,
  input  in_42,
  input  in_43,
  input  in_44,
  input  in_45,
  input  in_46,
  input  in_47,
  input  in_48,
  input  in_49,
  input  in_50,
  input  in_51,
  input  in_52,
  input  in_53,
  input  in_54,
  input  in_55,
  input  in_56,
  input  in_57,
  input  in_58,
  input  in_59,
  input  in_60,
  input  in_61,
  input  in_62,
  input  in_63,
  input  in_64,
  output out_65,
  output out_66,
  output out_67,
  output out_68,
  output out_69,
  output out_70,
  output out_71,
  output out_72,
  output out_73,
  output out_74,
  output out_75,
  output out_76,
  output out_77,
  output out_78,
  output out_79,
  output out_80,
  output out_81,
  output out_82,
  output out_83,
  output out_84,
  output out_85,
  output out_86,
  output out_87,
  output out_88,
  output out_89,
  output out_90,
  output out_91,
  output out_92,
  output out_93,
  output out_94,
  output out_95,
  output out_96
);

  wire golo_1_out_8, golo_2_out_8, golo_3_out_8, golo_4_out_8, golo_5_out_8, golo_6_out_8, golo_7_out_8,
       golo_8_out_8, golo_9_out_8, golo_10_out_8, golo_11_out_8, golo_12_out_8, golo_13_out_8, golo_14_out_8,
       golo_15_out_8, golo_16_out_8, golo_17_out_8, golo_18_out_8, golo_19_out_8, golo_20_out_8,
       golo_21_out_8, golo_22_out_8, golo_23_out_8, golo_24_out_8, golo_25_out_8, golo_26_out_8,
       golo_27_out_8, golo_28_out_8, golo_29_out_8, golo_30_out_8, or_1_out, ult_1_out_8;

  golo golo_1 (
    .a(in_3), .b(in_4), .bi(Bnegate), .crri(Bnegate), .less(ult_1_out_8), .op(OP), .out_7(out_65),
    .out_8(golo_1_out_8));
  golo golo_2 (
    .a(in_5), .b(in_6), .bi(Bnegate), .crri(golo_1_out_8), .less(1'b0), .op(OP), .out_7(out_66),
    .out_8(golo_2_out_8));
  golo golo_3 (
    .a(in_7), .b(in_8), .bi(Bnegate), .crri(golo_2_out_8), .less(1'b0), .op(OP), .out_7(out_67),
    .out_8(golo_3_out_8));
  golo golo_4 (
    .a(in_9), .b(in_10), .bi(Bnegate), .crri(golo_3_out_8), .less(1'b0), .op(OP), .out_7(out_68),
    .out_8(golo_4_out_8));
  golo golo_5 (
    .a(in_11), .b(in_12), .bi(Bnegate), .crri(golo_4_out_8), .less(1'b0), .op(OP), .out_7(out_69),
    .out_8(golo_5_out_8));
  golo golo_6 (
    .a(in_13), .b(in_14), .bi(Bnegate), .crri(golo_5_out_8), .less(1'b0), .op(OP), .out_7(out_70),
    .out_8(golo_6_out_8));
  golo golo_7 (
    .a(in_15), .b(in_16), .bi(Bnegate), .crri(golo_6_out_8), .less(1'b0), .op(OP), .out_7(out_71),
    .out_8(golo_7_out_8));
  golo golo_8 (
    .a(in_17), .b(in_18), .bi(Bnegate), .crri(golo_7_out_8), .less(1'b0), .op(OP), .out_7(out_72),
    .out_8(golo_8_out_8));
  golo golo_9 (
    .a(in_19), .b(in_20), .bi(Bnegate), .crri(golo_8_out_8), .less(1'b0), .op(OP), .out_7(out_73),
    .out_8(golo_9_out_8));
  golo golo_10 (
    .a(in_21), .b(in_22), .bi(Bnegate), .crri(golo_9_out_8), .less(1'b0), .op(OP), .out_7(out_74),
    .out_8(golo_10_out_8));
  golo golo_11 (
    .a(in_23), .b(in_24), .bi(Bnegate), .crri(golo_10_out_8), .less(1'b0), .op(OP), .out_7(out_75),
    .out_8(golo_11_out_8));
  golo golo_12 (
    .a(in_25), .b(in_26), .bi(Bnegate), .crri(golo_11_out_8), .less(1'b0), .op(OP), .out_7(out_76),
    .out_8(golo_12_out_8));
  golo golo_13 (
    .a(in_27), .b(in_28), .bi(Bnegate), .crri(golo_12_out_8), .less(1'b0), .op(OP), .out_7(out_77),
    .out_8(golo_13_out_8));
  golo golo_14 (
    .a(in_29), .b(in_30), .bi(Bnegate), .crri(golo_13_out_8), .less(1'b0), .op(OP), .out_7(out_78),
    .out_8(golo_14_out_8));
  golo golo_15 (
    .a(in_31), .b(in_32), .bi(Bnegate), .crri(golo_14_out_8), .less(1'b0), .op(OP), .out_7(out_79),
    .out_8(golo_15_out_8));
  golo golo_16 (
    .a(in_33), .b(in_34), .bi(Bnegate), .crri(golo_15_out_8), .less(1'b0), .op(OP), .out_7(out_80),
    .out_8(golo_16_out_8));
  golo golo_17 (
    .a(in_35), .b(in_36), .bi(Bnegate), .crri(golo_16_out_8), .less(1'b0), .op(OP), .out_7(out_82),
    .out_8(golo_17_out_8));
  golo golo_18 (
    .a(in_37), .b(in_38), .bi(Bnegate), .crri(golo_17_out_8), .less(1'b0), .op(OP), .out_7(out_83),
    .out_8(golo_18_out_8));
  golo golo_19 (
    .a(in_39), .b(in_40), .bi(Bnegate), .crri(golo_18_out_8), .less(1'b0), .op(OP), .out_7(out_84),
    .out_8(golo_19_out_8));
  golo golo_20 (
    .a(in_41), .b(in_42), .bi(Bnegate), .crri(golo_19_out_8), .less(1'b0), .op(OP), .out_7(out_85),
    .out_8(golo_20_out_8));
  golo golo_21 (
    .a(in_43), .b(in_44), .bi(Bnegate), .crri(golo_20_out_8), .less(1'b0), .op(OP), .out_7(out_86),
    .out_8(golo_21_out_8));
  golo golo_22 (
    .a(in_45), .b(in_46), .bi(Bnegate), .crri(golo_21_out_8), .less(1'b0), .op(OP), .out_7(out_87),
    .out_8(golo_22_out_8));
  golo golo_23 (
    .a(in_47), .b(in_48), .bi(Bnegate), .crri(golo_22_out_8), .less(1'b0), .op(OP), .out_7(out_88),
    .out_8(golo_23_out_8));
  golo golo_24 (
    .a(in_49), .b(in_50), .bi(Bnegate), .crri(golo_23_out_8), .less(1'b0), .op(OP), .out_7(out_89),
    .out_8(golo_24_out_8));
  golo golo_25 (
    .a(in_51), .b(in_52), .bi(Bnegate), .crri(golo_24_out_8), .less(1'b0), .op(OP), .out_7(out_90),
    .out_8(golo_25_out_8));
  golo golo_26 (
    .a(in_53), .b(in_54), .bi(Bnegate), .crri(golo_25_out_8), .less(1'b0), .op(OP), .out_7(out_91),
    .out_8(golo_26_out_8));
  golo golo_27 (
    .a(in_55), .b(in_56), .bi(Bnegate), .crri(golo_26_out_8), .less(1'b0), .op(OP), .out_7(out_92),
    .out_8(golo_27_out_8));
  golo golo_28 (
    .a(in_57), .b(in_58), .bi(Bnegate), .crri(golo_27_out_8), .less(1'b0), .op(OP), .out_7(out_93),
    .out_8(golo_28_out_8));
  golo golo_29 (
    .a(in_59), .b(in_60), .bi(Bnegate), .crri(golo_28_out_8), .less(1'b0), .op(OP), .out_7(out_94),
    .out_8(golo_29_out_8));
  golo golo_30 (
    .a(in_61), .b(in_62), .bi(Bnegate), .crri(golo_29_out_8), .less(1'b0), .op(OP), .out_7(out_95),
    .out_8(golo_30_out_8));
  ult ult_1 (
    .a(in_63), .b(in_64), .bI(Bnegate), .crri(golo_30_out_8), .less(1'b0), .op(OP), .out_7(out_96),
    .out_8(ult_1_out_8));
  or or_1 (or_1_out, out_65, out_66, out_67, out_68, out_69, out_70, out_71, out_72, out_73, out_74, out_75, out_76, out_77, out_78, out_79, out_80, out_82, out_83, out_84, out_85, out_86, out_87, out_88, out_89, out_90, out_91, out_92, out_93, out_94, out_95, out_96);
  not not_1 (out_81, or_1_out);
endmodule

module golo (
  input  a,
  input  b,
  input  bi,
  input  crri,
  input  less,
  input  [1:0] op,
  output out_7,
  output out_8
);

  wire adder_1_out, and_1_out, multiplexer_1_out, not_1_out, or_1_out;

  not not_1 (not_1_out, b);
  Multiplexer #(.enable("false")) multiplexer_1 (.in0(b), .in1(not_1_out), .out(multiplexer_1_out), .sel(bi));
  and and_1 (and_1_out, a, multiplexer_1_out);
  or or_1 (or_1_out, a, multiplexer_1_out);
  Adder #(.width(1)) adder_1 (.a(a), .b(multiplexer_1_out), .out(adder_1_out), .cin(crri), .cout(out_8));
  Multiplexer #(.select(2), .enable("false")) multiplexer_2 (
    .in0(and_1_out), .in1(or_1_out), .in2(adder_1_out), .in3(less), .out(out_7), .sel(op));
endmodule

module ult (
  input  a,
  input  b,
  input  bI,
  input  crri,
  input  less,
  input  [1:0] op,
  output out_7,
  output out_8
);

  wire and_1_out, multiplexer_1_out, not_1_out, or_1_out;

  not not_1 (not_1_out, b);
  Multiplexer #(.enable("false")) multiplexer_1 (.in0(b), .in1(not_1_out), .out(multiplexer_1_out), .sel(bI));
  and and_1 (and_1_out, a, multiplexer_1_out);
  or or_1 (or_1_out, a, multiplexer_1_out);
  Adder #(.width(1)) adder_1 (.a(a), .b(multiplexer_1_out), .out(out_8), .cin(crri));  // open: cout
  Multiplexer #(.select(2), .enable("false")) multiplexer_2 (
    .in0(and_1_out), .in1(or_1_out), .in2(out_8), .in3(less), .out(out_7), .sel(op));
endmodule

module ULA (
  input  in_1,
  input  [1:0] in_2,
  input  [31:0] in_3,
  input  [31:0] in_4,
  output [31:0] out_5,
  output out_6
);

  wire golo_1_out_8, golo_2_out_8, golo_3_out_8, golo_4_out_8, golo_5_out_8, golo_6_out_8, golo_7_out_8,
       golo_8_out_8, golo_9_out_8, golo_10_out_8, golo_11_out_8, golo_12_out_8, golo_13_out_8, golo_14_out_8,
       golo_15_out_8, golo_16_out_8, golo_17_out_8, golo_18_out_8, golo_19_out_8, golo_20_out_8,
       golo_21_out_8, golo_22_out_8, golo_23_out_8, golo_24_out_8, golo_25_out_8, golo_26_out_8,
       golo_27_out_8, golo_28_out_8, golo_29_out_8, golo_30_out_8, golo_31_out_8, ult_1_out_8;

  golo golo_1 (
    .a(in_3[0]), .b(in_4[0]), .bi(in_1), .crri(in_1), .less(ult_1_out_8), .op(in_2), .out_7(out_5[0]),
    .out_8(golo_1_out_8));
  golo golo_2 (
    .a(in_3[1]), .b(in_4[1]), .bi(in_1), .crri(golo_1_out_8), .less(1'b0), .op(in_2), .out_7(out_5[1]),
    .out_8(golo_2_out_8));
  golo golo_3 (
    .a(in_3[2]), .b(in_4[2]), .bi(in_1), .crri(golo_2_out_8), .less(1'b0), .op(in_2), .out_7(out_5[2]),
    .out_8(golo_3_out_8));
  golo golo_4 (
    .a(in_3[3]), .b(in_4[3]), .bi(in_1), .crri(golo_3_out_8), .less(1'b0), .op(in_2), .out_7(out_5[3]),
    .out_8(golo_4_out_8));
  golo golo_5 (
    .a(in_3[4]), .b(in_4[4]), .bi(in_1), .crri(golo_4_out_8), .less(1'b0), .op(in_2), .out_7(out_5[4]),
    .out_8(golo_5_out_8));
  golo golo_6 (
    .a(in_3[5]), .b(in_4[5]), .bi(in_1), .crri(golo_5_out_8), .less(1'b0), .op(in_2), .out_7(out_5[5]),
    .out_8(golo_6_out_8));
  golo golo_7 (
    .a(in_3[6]), .b(in_4[6]), .bi(in_1), .crri(golo_6_out_8), .less(1'b0), .op(in_2), .out_7(out_5[6]),
    .out_8(golo_7_out_8));
  golo golo_8 (
    .a(in_3[7]), .b(in_4[7]), .bi(in_1), .crri(golo_7_out_8), .less(1'b0), .op(in_2), .out_7(out_5[7]),
    .out_8(golo_8_out_8));
  golo golo_9 (
    .a(in_3[8]), .b(in_4[8]), .bi(in_1), .crri(golo_8_out_8), .less(1'b0), .op(in_2), .out_7(out_5[8]),
    .out_8(golo_9_out_8));
  golo golo_10 (
    .a(in_3[9]), .b(in_4[9]), .bi(in_1), .crri(golo_9_out_8), .less(1'b0), .op(in_2), .out_7(out_5[9]),
    .out_8(golo_10_out_8));
  golo golo_11 (
    .a(in_3[10]), .b(in_4[10]), .bi(in_1), .crri(golo_10_out_8), .less(1'b0), .op(in_2), .out_7(out_5[10]),
    .out_8(golo_11_out_8));
  golo golo_12 (
    .a(in_3[11]), .b(in_4[11]), .bi(in_1), .crri(golo_11_out_8), .less(1'b0), .op(in_2), .out_7(out_5[11]),
    .out_8(golo_12_out_8));
  golo golo_13 (
    .a(in_3[12]), .b(in_4[12]), .bi(in_1), .crri(golo_12_out_8), .less(1'b0), .op(in_2), .out_7(out_5[12]),
    .out_8(golo_13_out_8));
  golo golo_14 (
    .a(in_3[13]), .b(in_4[13]), .bi(in_1), .crri(golo_13_out_8), .less(1'b0), .op(in_2), .out_7(out_5[13]),
    .out_8(golo_14_out_8));
  golo golo_15 (
    .a(in_3[14]), .b(in_4[14]), .bi(in_1), .crri(golo_14_out_8), .less(1'b0), .op(in_2), .out_7(out_5[14]),
    .out_8(golo_15_out_8));
  golo golo_16 (
    .a(in_3[15]), .b(in_4[15]), .bi(in_1), .crri(golo_15_out_8), .less(1'b0), .op(in_2), .out_7(out_5[15]),
    .out_8(golo_16_out_8));
  golo golo_17 (
    .a(in_3[16]), .b(in_4[16]), .bi(in_1), .crri(golo_16_out_8), .less(1'b0), .op(in_2), .out_7(out_5[16]),
    .out_8(golo_17_out_8));
  golo golo_18 (
    .a(in_3[17]), .b(in_4[17]), .bi(in_1), .crri(golo_17_out_8), .less(1'b0), .op(in_2), .out_7(out_5[17]),
    .out_8(golo_18_out_8));
  golo golo_19 (
    .a(in_3[18]), .b(in_4[18]), .bi(in_1), .crri(golo_18_out_8), .less(1'b0), .op(in_2), .out_7(out_5[18]),
    .out_8(golo_19_out_8));
  golo golo_20 (
    .a(in_3[19]), .b(in_4[19]), .bi(in_1), .crri(golo_19_out_8), .less(1'b0), .op(in_2), .out_7(out_5[19]),
    .out_8(golo_20_out_8));
  golo golo_21 (
    .a(in_3[20]), .b(in_4[20]), .bi(in_1), .crri(golo_20_out_8), .less(1'b0), .op(in_2), .out_7(out_5[20]),
    .out_8(golo_21_out_8));
  golo golo_22 (
    .a(in_3[21]), .b(in_4[21]), .bi(in_1), .crri(golo_21_out_8), .less(1'b0), .op(in_2), .out_7(out_5[21]),
    .out_8(golo_22_out_8));
  golo golo_23 (
    .a(in_3[22]), .b(in_4[22]), .bi(in_1), .crri(golo_22_out_8), .less(1'b0), .op(in_2), .out_7(out_5[22]),
    .out_8(golo_23_out_8));
  golo golo_24 (
    .a(in_3[23]), .b(in_4[23]), .bi(in_1), .crri(golo_23_out_8), .less(1'b0), .op(in_2), .out_7(out_5[23]),
    .out_8(golo_24_out_8));
  golo golo_25 (
    .a(in_3[24]), .b(in_4[24]), .bi(in_1), .crri(golo_24_out_8), .less(1'b0), .op(in_2), .out_7(out_5[24]),
    .out_8(golo_25_out_8));
  golo golo_26 (
    .a(in_3[25]), .b(in_4[25]), .bi(in_1), .crri(golo_25_out_8), .less(1'b0), .op(in_2), .out_7(out_5[25]),
    .out_8(golo_26_out_8));
  golo golo_27 (
    .a(in_3[26]), .b(in_4[26]), .bi(in_1), .crri(golo_26_out_8), .less(1'b0), .op(in_2), .out_7(out_5[26]),
    .out_8(golo_27_out_8));
  golo golo_28 (
    .a(in_3[27]), .b(in_4[27]), .bi(in_1), .crri(golo_27_out_8), .less(1'b0), .op(in_2), .out_7(out_5[27]),
    .out_8(golo_28_out_8));
  golo golo_29 (
    .a(in_3[28]), .b(in_4[28]), .bi(in_1), .crri(golo_28_out_8), .less(1'b0), .op(in_2), .out_7(out_5[28]),
    .out_8(golo_29_out_8));
  golo golo_30 (
    .a(in_3[29]), .b(in_4[29]), .bi(in_1), .crri(golo_29_out_8), .less(1'b0), .op(in_2), .out_7(out_5[29]),
    .out_8(golo_30_out_8));
  golo golo_31 (
    .a(in_3[30]), .b(in_4[30]), .bi(in_1), .crri(golo_30_out_8), .less(1'b0), .op(in_2), .out_7(out_5[30]),
    .out_8(golo_31_out_8));
  ult ult_1 (
    .a(in_3[31]), .b(in_4[31]), .bI(in_1), .crri(golo_31_out_8), .less(1'b0), .op(in_2), .out_7(out_5[31]),
    .out_8(ult_1_out_8));
  nor nor_1 (out_6, out_5[0], out_5[1], out_5[2], out_5[3], out_5[4], out_5[5], out_5[6], out_5[7], out_5[8], out_5[9], out_5[10], out_5[11], out_5[12], out_5[13], out_5[14], out_5[15], out_5[16], out_5[17], out_5[18], out_5[19], out_5[20], out_5[21], out_5[22], out_5[23], out_5[24], out_5[25], out_5[26], out_5[27], out_5[28], out_5[29], out_5[30], out_5[31]);

  // Notes on the sheet:
  //   A
  //   B
endmodule

module teste (
  input  [1:0] in_1,
  input  in_2,
  input  [31:0] in_3,
  input  [31:0] in_4,
  output [31:0] out_5,
  output out_6
);

  // ULA ula_1: pin names not known; wires that end beside it: in_1, in_2, in_3, in_4, out_5, out_6
endmodule
