// Logisim project control.circ as structural Verilog: 1 circuit, main circuit main
module main (
  input  [5:0] in_1,
  output out_2,
  output out_3,
  output out_4,
  output out_5,
  output out_6,
  output out_7,
  output out_8,
  output out_9,
  output out_10
);

  wire not_1_out, not_2_out, not_3_out, not_4_out, not_5_out, not_6_out, not_7_out, not_8_out, not_9_out,
       not_10_out, not_11_out, not_12_out, not_13_out, not_14_out, not_15_out, not_16_out;

  not not_1 (not_1_out, in_1[5]);
  not not_2 (not_2_out, in_1[4]);
  not not_3 (not_3_out, in_1[2]);
  not not_4 (not_4_out, in_1[1]);
  not not_5 (not_5_out, in_1[4]);
  not not_6 (not_6_out, in_1[3]);
  not not_7 (not_7_out, in_1[0]);
  and and_1 (out_2, not_1_out, not_2_out, not_6_out, not_3_out, not_4_out, not_7_out);
  not not_8 (not_8_out, in_1[3]);
  not not_9 (not_9_out, in_1[2]);
  not not_10 (not_10_out, in_1[4]);
  and and_2 (out_4, in_1[5], not_5_out, not_8_out, not_9_out, in_1[1], in_1[0]);
  not not_11 (not_11_out, in_1[2]);
  not not_12 (not_12_out, in_1[5]);
  not not_13 (not_13_out, in_1[4]);
  and and_3 (out_7, in_1[5], not_10_out, in_1[3], not_11_out, in_1[1], in_1[0]);
  not not_14 (not_14_out, in_1[1]);
  not not_15 (not_15_out, in_1[3]);
  not not_16 (not_16_out, in_1[0]);
  and and_4 (out_8, not_12_out, not_13_out, not_15_out, in_1[2], not_14_out, not_16_out);
  or or_1 (out_3, out_4, out_7);
  or or_2 (out_5, out_2, out_4);

  assign out_6 = out_4;
  assign out_9 = out_2;
  assign out_10 = out_8;
endmodule
