// Logisim project dist.circ as structural Verilog: 1 circuit, main circuit main
module main (
  input  [31:0] in_1,
  output [5:0] out_2,
  output [4:0] out_3,
  output [4:0] out_4,
  output [15:0] out_5
);


  assign out_2 = in_1[31:26];
  assign out_3 = in_1[20:16];
  assign out_4 = in_1[25:21];
  assign out_5 = in_1[15:0];
endmodule
