// Logisim project dist2.circ as structural Verilog: 1 circuit, main circuit main
module main (
  input  [15:0] in_1,
  output [4:0] out_2,
  output [5:0] out_3
);


  assign out_2 = in_1[15:11];
  assign out_3 = in_1[5:0];
endmodule
