// Logisim project memoria.circ as structural Verilog: 2 circuits, main circuit Instruction Memory
module Instruction_Memory (
  input  [31:0] Read_Address,
  output [31:0] Instruction
);

  RAM #(.addrWidth(12), .dataWidth(32)) ram_1 (
    .addr(Read_Address[13:2]), .data(Instruction));  // open: sel, clk, ld, clr
endmodule

module Data_Memory (
  input  Mem_Write,
  input  [31:0] Address,
  input  [31:0] Write_Data,
  input  Read_Enable,
  output [31:0] Read_Data
);

  wire clock_1_out, not_1_out, or_1_out;

  assign Read_Data = Mem_Write ? Write_Data : 32'bz;  // Controlled_Buffer controlled_buffer_1
  not not_1 (not_1_out, Mem_Write);
  or or_1 (or_1_out, not_1_out, Read_Enable);
  RAM #(.addrWidth(12), .dataWidth(32)) ram_1 (
    .addr(Address[13:2]), .data(Read_Data), .clk(clock_1_out), .ld(or_1_out));  // open: sel, clr
  Clock clock_1 (.out(clock_1_out));
endmodule
