// Logisim project mips.circ as structural Verilog
// instruction memory
module monociclo (
  input  in_1,
  output [5:0] out_2
);

  wire and_1_out, clock_out, Control_out_2, Control_out_3, Control_out_4, Control_out_5, Control_out_6,
       Control_out_7, Control_out_8, Control_out_9, Control_out_10, ULA_control_out_4, ULA_out_6;
  wire [1:0] ULA_control_out_5;
  wire [4:0] dist_2_out_2, distribuidor_out_3, distribuidor_out_4, multiplexer_1_out;
  wire [5:0] distribuidor_out_2;
  wire [15:0] distribuidor_out_5;
  wire [31:0] add_2_out_3, add_out_2, counter_1_q, data_memory_1_read_data, extensor_out_2,
       instruction_memory_1_instruction, multiplexer_2_out, multiplexer_3_out, multiplexer_4_out,
       n32_register_file_1_read_data_1, n32_register_file_1_read_data_2, sift_left_p2, ULA_out_5;

  Counter #(.width(32), .max('hffffffff)) counter_1 (
    .load(1'b1), .D(multiplexer_3_out), .count(1'b0), .Q(counter_1_q), .clk(clock_out), .clr(in_1));  // open: carry
  Clock clock (.out(clock_out));
  Instruction_Memory instruction_memory_1 (.Read_Address(counter_1_q), .Instruction(instruction_memory_1_instruction));
  dist_main distribuidor (
    .in_1(instruction_memory_1_instruction), .out_2(distribuidor_out_2), .out_3(distribuidor_out_3),
    .out_4(distribuidor_out_4), .out_5(distribuidor_out_5));
  add_main add (.in_1(counter_1_q), .out_2(add_out_2));
  control_main Control (
    .in_1(distribuidor_out_2), .out_2(Control_out_2), .out_3(Control_out_3), .out_4(Control_out_4),
    .out_5(Control_out_5), .out_6(Control_out_6), .out_7(Control_out_7), .out_8(Control_out_8),
    .out_9(Control_out_9), .out_10(Control_out_10));
  dist2_main dist_2 (.in_1(distribuidor_out_5), .out_2(dist_2_out_2), .out_3(out_2));
  Multiplexer #(.width(5), .enable("false")) multiplexer_1 (
    .in0(distribuidor_out_4), .in1(dist_2_out_2), .out(multiplexer_1_out), .sel(Control_out_2));
  _16_32 extensor (.in_1(distribuidor_out_5), .out_2(extensor_out_2));
  _32_register_file u_32_register_file_1 (
    .Read_Register_1(distribuidor_out_3), .Read_Register_2(distribuidor_out_4),
    .Write_Register(multiplexer_1_out), .Write_Data_2(multiplexer_4_out), .Write_Data(Control_out_5),
    .Read_data_1(n32_register_file_1_read_data_1), .Read_Data_2(n32_register_file_1_read_data_2));
  Multiplexer #(.width(32), .enable("false")) multiplexer_2 (
    .in0(n32_register_file_1_read_data_2), .in1(extensor_out_2), .out(multiplexer_2_out), .sel(Control_out_3));
  ula_control_main ULA_control (
    .in_3(out_2), .in_1(Control_out_9), .in_2(Control_out_10), .out_4(ULA_control_out_4),
    .out_5(ULA_control_out_5));
  // SL_main sift_left: pin names not known; wires that end beside it: extensor_out_2, sift_left_p2
  add2 add_2 (.in_1(add_out_2), .in_2(sift_left_p2), .out_3(add_2_out_3));
  and and_1 (and_1_out, Control_out_8, ULA_out_6);
  ULA ULA (
    .in_1(ULA_control_out_4), .in_2(ULA_control_out_5), .in_3(n32_register_file_1_read_data_1),
    .in_4(multiplexer_2_out), .out_5(ULA_out_5), .out_6(ULA_out_6));
  Multiplexer #(.width(32), .enable("false")) multiplexer_3 (
    .in0(add_out_2), .in1(add_2_out_3), .out(multiplexer_3_out), .sel(and_1_out));
  Data_Memory data_memory_1 (
    .Address(ULA_out_5), .Write_Data(multiplexer_2_out), .Mem_Write(Control_out_7),
    .Read_Enable(Control_out_6), .Read_Data(data_memory_1_read_data));
  Multiplexer #(.width(32), .enable("false")) multiplexer_4 (
    .in0(data_memory_1_read_data), .in1(ULA_out_5), .out(multiplexer_4_out), .sel(Control_out_4));

  // Notes on the sheet:
  //   instruction memory
endmodule

module _16_32 (
  input  [15:0] in_1,
  output [31:0] out_2
);


  assign out_2 = {{16{1'b0}}, in_1};
endmodule
