// Logisim project outroscomponentes.circ as structural Verilog: 2 circuits, main circuit 5_sel_decoder
module _5_sel_decoder (
  input  [4:0] in_1,
  output [31:0] out_2
);

  wire [15:0] decoder_2_out0, decoder_3_out0;
  wire [15:15] decoder_1_out0, decoder_1_out1;

  Decoder #(.select(1), .tristate("false")) decoder_1 (
    .out0(decoder_1_out0[15]), .out1(decoder_1_out1[15]), .sel(in_1[4]));
  Decoder #(.select(4), .tristate("false")) decoder_2 (
    .out0(decoder_2_out0[0]), .out1(decoder_2_out0[1]), .out2(decoder_2_out0[2]), .out3(decoder_2_out0[3]),
    .out4(decoder_2_out0[4]), .out5(decoder_2_out0[5]), .out6(decoder_2_out0[6]), .out7(decoder_2_out0[7]),
    .out8(decoder_2_out0[8]), .out9(decoder_2_out0[9]), .out10(decoder_2_out0[10]),
    .out11(decoder_2_out0[11]), .out12(decoder_2_out0[12]), .out13(decoder_2_out0[13]),
    .out14(decoder_2_out0[14]), .out15(decoder_2_out0[15]), .sel(in_1[3:0]));
  Decoder #(.select(4), .tristate("false")) decoder_3 (
    .out0(decoder_3_out0[0]), .out1(decoder_3_out0[1]), .out2(decoder_3_out0[2]), .out3(decoder_3_out0[3]),
    .out4(decoder_3_out0[4]), .out5(decoder_3_out0[5]), .out6(decoder_3_out0[6]), .out7(decoder_3_out0[7]),
    .out8(decoder_3_out0[8]), .out9(decoder_3_out0[9]), .out10(decoder_3_out0[10]),
    .out11(decoder_3_out0[11]), .out12(decoder_3_out0[12]), .out13(decoder_3_out0[13]),
    .out14(decoder_3_out0[14]), .out15(decoder_3_out0[15]), .sel(in_1[3:0]));
  assign out_2[15:0] = decoder_2_out0 & {16{decoder_1_out0[15]}};  // AND_Gate and_1, 16 bits wide
  assign out_2[31:16] = decoder_3_out0 & {16{decoder_1_out1[15]}};  // AND_Gate and_2, 16 bits wide
endmodule

module _5_sel_mux (
  input  [31:0] in_1,
  input  [31:0] in_2,
  input  [31:0] in_3,
  input  [31:0] in_4,
  input  [31:0] in_5,
  input  [31:0] in_6,
  input  [31:0] in_7,
  input  [31:0] in_8,
  input  [31:0] in_9,
  input  [31:0] in_10,
  input  [31:0] in_11,
  input  [31:0] in_12,
  input  [31:0] in_13,
  input  [31:0] in_14,
  input  [31:0] in_15,
  input  [31:0] in_16,
  input  [31:0] in_17,
  input  [31:0] in_18,
  input  [31:0] in_19,
  input  [31:0] in_20,
  input  [31:0] in_21,
  input  [31:0] in_22,
  input  [31:0] in_23,
  input  [31:0] in_24,
  input  [31:0] in_25,
  input  [31:0] in_26,
  input  [31:0] in_27,
  input  [31:0] in_28,
  input  [31:0] in_29,
  input  [31:0] in_30,
  input  [31:0] in_31,
  input  [31:0] in_32,
  input  [4:0] in_33,
  output [31:0] out_34
);

  wire [31:0] multiplexer_1_out, multiplexer_2_out;

  Multiplexer #(.select(4), .width(32)) multiplexer_1 (
    .in0(in_1), .in1(in_2), .in2(in_3), .in3(in_4), .in4(in_5), .in5(in_6), .in6(in_7), .in7(in_8),
    .in8(in_9), .in9(in_10), .in10(in_11), .in11(in_12), .in12(in_13), .in13(in_14), .in14(in_15),
    .in15(in_16), .out(multiplexer_1_out), .sel(in_33[3:0]));
  Multiplexer #(.select(4), .width(32)) multiplexer_2 (
    .in0(in_17), .in1(in_18), .in2(in_19), .in3(in_20), .in4(in_21), .in5(in_22), .in6(in_23), .in7(in_24),
    .in8(in_25), .in9(in_26), .in10(in_27), .in11(in_28), .in12(in_29), .in13(in_30), .in14(in_31),
    .in15(in_32), .out(multiplexer_2_out), .sel(in_33[3:0]));
  Multiplexer #(.select(1), .width(32)) multiplexer_3 (
    .in0(multiplexer_1_out), .in1(multiplexer_2_out), .out(out_34), .sel(in_33[4]));
endmodule
