// Logisim project registradores.circ as structural Verilog
module _4_register_section (
  input  [31:0] in_1,
  input  [3:0] dec_out,
  input  in_3,
  output [31:0] out_4,
  output [31:0] out_5,
  output [31:0] out_6,
  output [31:0] out_7
);

  wire and_1_out, and_2_out, and_3_out, and_4_out, clock_1_out, clock_2_out, clock_3_out, clock_4_out,
       not_1_out, not_2_out, not_3_out, not_4_out, or_1_out, or_2_out, or_3_out, or_4_out;

  Register #(.width(32)) register_1 (.D(in_1), .Q(out_4), .clk(or_1_out));  // open: en, clr
  or or_1 (or_1_out, not_1_out, clock_1_out);
  and and_1 (and_1_out, dec_out[0], in_3);
  not not_1 (not_1_out, and_1_out);
  Clock clock_1 (.out(clock_1_out));
  and and_2 (and_2_out, dec_out[1], in_3);
  Register #(.width(32)) register_2 (.D(in_1), .Q(out_5), .clk(or_2_out));  // open: en, clr
  or or_2 (or_2_out, not_2_out, clock_2_out);
  not not_2 (not_2_out, and_2_out);
  Clock clock_2 (.out(clock_2_out));
  or or_3 (or_3_out, not_3_out, clock_3_out);
  not not_3 (not_3_out, and_3_out);
  and and_3 (and_3_out, dec_out[2], in_3);
  Register #(.width(32)) register_3 (.D(in_1), .Q(out_6), .clk(or_3_out));  // open: en, clr
  Clock clock_3 (.out(clock_3_out));
  and and_4 (and_4_out, dec_out[3], in_3);
  Register #(.width(32)) register_4 (.D(in_1), .Q(out_7), .clk(or_4_out));  // open: en, clr
  or or_4 (or_4_out, not_4_out, clock_4_out);
  not not_4 (not_4_out, and_4_out);
  Clock clock_4 (.out(clock_4_out));

  // Notes on the sheet:
  //   Write Enable
endmodule

module _32_register_file (
  input  Write_Data,
  input  [4:0] Read_Register_1,
  input  [4:0] Read_Register_2,
  input  [4:0] Write_Register,
  input  [31:0] Write_Data_2,
  output [31:0] Read_data_1,
  output [31:0] Read_Data_2
);

  wire [31:0] n4_register_section_1_out_4, n4_register_section_1_out_5, n4_register_section_1_out_6,
       n4_register_section_1_out_7, n4_register_section_2_out_4, n4_register_section_2_out_5,
       n4_register_section_2_out_6, n4_register_section_2_out_7, n4_register_section_3_out_4,
       n4_register_section_3_out_5, n4_register_section_3_out_6, n4_register_section_3_out_7,
       n4_register_section_4_out_4, n4_register_section_4_out_5, n4_register_section_4_out_6,
       n4_register_section_4_out_7, n4_register_section_5_out_4, n4_register_section_5_out_5,
       n4_register_section_5_out_6, n4_register_section_5_out_7, n4_register_section_6_out_4,
       n4_register_section_6_out_5, n4_register_section_6_out_6, n4_register_section_6_out_7,
       n4_register_section_7_out_4, n4_register_section_7_out_5, n4_register_section_7_out_6,
       n4_register_section_7_out_7, n4_register_section_8_out_4, n4_register_section_8_out_5,
       n4_register_section_8_out_6, n4_register_section_8_out_7, n5_sel_decoder_1_out_2;

  _5_sel_decoder u_5_sel_decoder_1 (.in_1(Write_Register), .out_2(n5_sel_decoder_1_out_2));
  _4_register_section u_4_register_section_1 (
    .in_1(Write_Data_2), .dec_out(n5_sel_decoder_1_out_2[3:0]), .in_3(Write_Data),
    .out_4(n4_register_section_1_out_4), .out_5(n4_register_section_1_out_5),
    .out_6(n4_register_section_1_out_6), .out_7(n4_register_section_1_out_7));
  _4_register_section u_4_register_section_2 (
    .in_1(Write_Data_2), .dec_out(n5_sel_decoder_1_out_2[11:8]), .in_3(Write_Data),
    .out_4(n4_register_section_2_out_4), .out_5(n4_register_section_2_out_5),
    .out_6(n4_register_section_2_out_6), .out_7(n4_register_section_2_out_7));
  _4_register_section u_4_register_section_3 (
    .in_1(Write_Data_2), .dec_out(n5_sel_decoder_1_out_2[19:16]), .in_3(Write_Data),
    .out_4(n4_register_section_3_out_4), .out_5(n4_register_section_3_out_5),
    .out_6(n4_register_section_3_out_6), .out_7(n4_register_section_3_out_7));
  _4_register_section u_4_register_section_4 (
    .in_1(Write_Data_2), .dec_out(n5_sel_decoder_1_out_2[27:24]), .in_3(Write_Data),
    .out_4(n4_register_section_4_out_4), .out_5(n4_register_section_4_out_5),
    .out_6(n4_register_section_4_out_6), .out_7(n4_register_section_4_out_7));
  _4_register_section u_4_register_section_5 (
    .in_1(Write_Data_2), .dec_out(n5_sel_decoder_1_out_2[7:4]), .in_3(Write_Data),
    .out_4(n4_register_section_5_out_4), .out_5(n4_register_section_5_out_5),
    .out_6(n4_register_section_5_out_6), .out_7(n4_register_section_5_out_7));
  _4_register_section u_4_register_section_6 (
    .in_1(Write_Data_2), .dec_out(n5_sel_decoder_1_out_2[15:12]), .in_3(Write_Data),
    .out_4(n4_register_section_6_out_4), .out_5(n4_register_section_6_out_5),
    .out_6(n4_register_section_6_out_6), .out_7(n4_register_section_6_out_7));
  _4_register_section u_4_register_section_7 (
    .in_1(Write_Data_2), .dec_out(n5_sel_decoder_1_out_2[23:20]), .in_3(Write_Data),
    .out_4(n4_register_section_7_out_4), .out_5(n4_register_section_7_out_5),
    .out_6(n4_register_section_7_out_6), .out_7(n4_register_section_7_out_7));
  _4_register_section u_4_register_section_8 (
    .in_1(Write_Data_2), .dec_out(n5_sel_decoder_1_out_2[31:28]), .in_3(Write_Data),
    .out_4(n4_register_section_8_out_4), .out_5(n4_register_section_8_out_5),
    .out_6(n4_register_section_8_out_6), .out_7(n4_register_section_8_out_7));
  _5_sel_mux u_5_sel_mux_1 (
    .in_1(n4_register_section_1_out_4), .in_2(n4_register_section_1_out_5),
    .in_3(n4_register_section_1_out_6), .in_4(n4_register_section_1_out_7),
    .in_5(n4_register_section_5_out_4), .in_6(n4_register_section_5_out_5),
    .in_7(n4_register_section_5_out_6), .in_8(n4_register_section_5_out_7),
    .in_9(n4_register_section_2_out_4), .in_10(n4_register_section_2_out_5),
    .in_11(n4_register_section_2_out_6), .in_12(n4_register_section_2_out_7),
    .in_13(n4_register_section_6_out_4), .in_14(n4_register_section_6_out_5),
    .in_15(n4_register_section_6_out_6), .in_16(n4_register_section_6_out_7),
    .in_17(n4_register_section_3_out_4), .in_18(n4_register_section_3_out_5),
    .in_19(n4_register_section_3_out_6), .in_20(n4_register_section_3_out_7),
    .in_21(n4_register_section_7_out_4), .in_22(n4_register_section_7_out_5),
    .in_23(n4_register_section_7_out_6), .in_24(n4_register_section_7_out_7),
    .in_25(n4_register_section_4_out_4), .in_26(n4_register_section_4_out_5),
    .in_27(n4_register_section_4_out_6), .in_28(n4_register_section_4_out_7),
    .in_29(n4_register_section_8_out_4), .in_30(n4_register_section_8_out_5),
    .in_31(n4_register_section_8_out_6), .in_32(n4_register_section_8_out_7), .in_33(Read_Register_1),
    .out_34(Read_data_1));
  _5_sel_mux u_5_sel_mux_2 (
    .in_1(n4_register_section_1_out_4), .in_2(n4_register_section_1_out_5),
    .in_3(n4_register_section_1_out_6), .in_4(n4_register_section_1_out_7),
    .in_5(n4_register_section_5_out_4), .in_6(n4_register_section_5_out_5),
    .in_7(n4_register_section_5_out_6), .in_8(n4_register_section_5_out_7),
    .in_9(n4_register_section_2_out_4), .in_10(n4_register_section_2_out_5),
    .in_11(n4_register_section_2_out_6), .in_12(n4_register_section_2_out_7),
    .in_13(n4_register_section_6_out_4), .in_14(n4_register_section_6_out_5),
    .in_15(n4_register_section_6_out_6), .in_16(n4_register_section_6_out_7),
    .in_17(n4_register_section_3_out_4), .in_18(n4_register_section_3_out_5),
    .in_19(n4_register_section_3_out_6), .in_20(n4_register_section_3_out_7),
    .in_21(n4_register_section_7_out_4), .in_22(n4_register_section_7_out_5),
    .in_23(n4_register_section_7_out_6), .in_24(n4_register_section_7_out_7),
    .in_25(n4_register_section_4_out_4), .in_26(n4_register_section_4_out_5),
    .in_27(n4_register_section_4_out_6), .in_28(n4_register_section_4_out_7),
    .in_29(n4_register_section_8_out_4), .in_30(n4_register_section_8_out_5),
    .in_31(n4_register_section_8_out_6), .in_32(n4_register_section_8_out_7), .in_33(Read_Register_2),
    .out_34(Read_Data_2));
endmodule
