// Logisim project ula control.circ as structural Verilog: 1 circuit, main circuit main
module main (
  input  in_1,
  input  in_2,
  input  [5:0] in_3,
  output out_4,
  output [1:0] out_5
);

  wire and_1_out, not_1_out, not_2_out, or_1_out;

  or or_1 (or_1_out, in_3[3], in_3[0]);
  and and_1 (and_1_out, in_1, in_3[1]);
  and and_2 (out_5[0], in_1, or_1_out);
  not not_1 (not_1_out, in_1);
  not not_2 (not_2_out, in_3[2]);
  or or_2 (out_4, in_2, and_1_out);
  or or_3 (out_5[1], not_1_out, not_2_out);
endmodule
