// Logisim project somador_copia.circ as structural Verilog: 4 circuits, main circuit SomadorQuirino
module SomadorQuirino (
  input  in_1,
  input  in_2,
  input  in_3,
  input  in_4,
  input  in_5,
  input  in_6,
  input  in_7,
  input  in_8,
  input  in_9,
  input  in_10,
  input  in_11,
  input  in_12,
  input  in_13,
  input  in_14,
  input  in_15,
  input  in_16,
  input  in_17,
  input  in_18,
  input  in_19,
  input  in_20,
  input  in_21,
  input  in_22,
  input  in_23,
  input  in_24,
  output out_25,
  output out_26,
  output out_27,
  output out_28,
  output out_29,
  output out_30,
  output out_31,
  output out_32,
  output out_33,
  output out_34,
  output out_35,
  output out_36,
  output out_37
);

  Somador12Bits somador12bits_1 (
    .C0(out_36), .C2(out_34), .C4(out_32), .C6(out_30), .C8(out_28), .C10(out_26), .COUT(out_37), .A1(in_23),
    .A3(in_21), .B1(in_11), .B3(in_9), .A5(in_19), .A7(in_17), .B5(in_7), .B7(in_5), .A9(in_15), .A11(in_13),
    .B9(in_3), .B11(in_1), .CIN(1'b0), .B10(in_2), .B8(in_4), .A10(in_14), .A8(in_16), .B6(in_6), .B4(in_8),
    .A6(in_18), .A4(in_20), .B2(in_10), .B0(in_12), .A2(in_22), .A0(in_24), .C11(out_25), .C9(out_27),
    .C7(out_29), .C5(out_31), .C3(out_33), .C1(out_35));
endmodule

module Somador1Bit (
  input  A0,
  input  B0,
  input  CIN,
  output C0,
  output COUT
);

  wire and_1_out, and_2_out, and_3_out, xor_1_out;

  xor xor_1 (xor_1_out, A0, B0);
  and and_1 (and_1_out, A0, CIN);
  and and_2 (and_2_out, A0, B0);
  and and_3 (and_3_out, B0, CIN);
  xor xor_2 (C0, xor_1_out, CIN);
  or or_1 (COUT, and_1_out, and_2_out, and_3_out);
endmodule

module Somador4Bits (
  input  CIN,
  input  A0,
  input  B0,
  input  A1,
  input  B1,
  input  A2,
  input  B2,
  input  A3,
  input  B3,
  output C0,
  output C1,
  output C2,
  output C3,
  output COUT
);

  wire somador1bit_1_cout, somador1bit_2_cout, somador1bit_3_cout;

  Somador1Bit somador1bit_1 (.C0(C0), .CIN(CIN), .A0(A0), .B0(B0), .COUT(somador1bit_1_cout));
  Somador1Bit somador1bit_2 (.C0(C1), .CIN(somador1bit_1_cout), .A0(A1), .B0(B1), .COUT(somador1bit_2_cout));
  Somador1Bit somador1bit_3 (.C0(C2), .CIN(somador1bit_2_cout), .A0(A2), .B0(B2), .COUT(somador1bit_3_cout));
  Somador1Bit somador1bit_4 (.C0(C3), .CIN(somador1bit_3_cout), .A0(A3), .B0(B3), .COUT(COUT));
endmodule

module Somador12Bits (
  input  A0,
  input  CIN,
  input  A1,
  input  A2,
  input  A3,
  input  B0,
  input  B1,
  input  B2,
  input  B3,
  input  A4,
  input  A5,
  input  A6,
  input  A7,
  input  B4,
  input  B5,
  input  B6,
  input  B7,
  input  A8,
  input  A9,
  input  A10,
  input  A11,
  input  B8,
  input  B9,
  input  B10,
  input  B11,
  output C0,
  output C1,
  output C2,
  output C3,
  output C4,
  output C5,
  output C6,
  output C7,
  output C8,
  output C9,
  output C10,
  output C11,
  output COUT
);

  wire somador4bits_1_cout, somador4bits_2_cout;

  Somador4Bits somador4bits_1 (
    .C0(C0), .C2(C2), .COUT(somador4bits_1_cout), .B0(B0), .B1(B1), .B2(B2), .B3(B3), .CIN(CIN), .A3(A3),
    .A2(A2), .A1(A1), .A0(A0), .C3(C3), .C1(C1));
  Somador4Bits somador4bits_2 (
    .C0(C4), .C2(C6), .COUT(somador4bits_2_cout), .B0(B4), .B1(B5), .B2(B6), .B3(B7),
    .CIN(somador4bits_1_cout), .A3(A7), .A2(A6), .A1(A5), .A0(A4), .C3(C7), .C1(C5));
  Somador4Bits somador4bits_3 (
    .C0(C8), .C2(C10), .COUT(COUT), .B0(B8), .B1(B9), .B2(B10), .B3(B11), .CIN(somador4bits_2_cout),
    .A3(A11), .A2(A10), .A1(A9), .A0(A8), .C3(C11), .C1(C9));
endmodule
