// Logisim project circuito.circ as structural Verilog: 3 circuits, main circuit main
module main (
  input  in_1,
  input  in_2,
  input  in_3,
  input  in_4,
  input  in_5,
  input  in_6,
  input  in_7,
  input  in_8,
  input  in_9,
  input  in_10,
  input  in_11,
  input  in_12,
  output out_13,
  output out_14,
  output out_15,
  output out_16,
  output out_17,
  output out_18,
  output out_19,
  output out_20,
  output out_21,
  output out_22,
  output out_23
);

  Reg11bits reg11bits_1 (
    .CLK(in_12), .In0(in_11), .Out0(out_23), .In1(in_10), .Out1(out_22), .In2(in_9), .Out2(out_21),
    .In3(in_8), .Out3(out_20), .In4(in_7), .Out4(out_19), .In5(in_6), .Out5(out_18), .In6(in_5),
    .Out6(out_17), .In7(in_4), .Out7(out_16), .In8(in_3), .Out8(out_15), .In9(in_2), .Out9(out_14),
    .In10(in_1), .Out10(out_13));
endmodule

module FlipFlopD (
  input  Data,
  input  CLK,
  output Q
);

  wire and_1_out, and_2_out, nor_2_out, not_1_out;

  not not_1 (not_1_out, Data);
  and and_1 (and_1_out, not_1_out, CLK);
  and and_2 (and_2_out, CLK, Data);
  nor nor_1 (Q, and_1_out, nor_2_out);
  nor nor_2 (nor_2_out, Q, and_2_out);
endmodule

module Reg11bits (
  input  In0,
  input  In1,
  input  In2,
  input  In3,
  input  In4,
  input  In5,
  input  In6,
  input  In7,
  input  In8,
  input  In9,
  input  In10,
  input  CLK,
  output Out0,
  output Out1,
  output Out2,
  output Out3,
  output Out4,
  output Out5,
  output Out6,
  output Out7,
  output Out8,
  output Out9,
  output Out10
);

  FlipFlopD flipflopd_1 (.Data(In0), .CLK(CLK), .Q(Out0));
  FlipFlopD flipflopd_2 (.Data(In1), .CLK(CLK), .Q(Out1));
  FlipFlopD flipflopd_3 (.Data(In2), .CLK(CLK), .Q(Out2));
  FlipFlopD flipflopd_4 (.Data(In3), .CLK(CLK), .Q(Out3));
  FlipFlopD flipflopd_5 (.Data(In4), .CLK(CLK), .Q(Out4));
  FlipFlopD flipflopd_6 (.Data(In5), .CLK(CLK), .Q(Out5));
  FlipFlopD flipflopd_7 (.Data(In6), .CLK(CLK), .Q(Out6));
  FlipFlopD flipflopd_8 (.Data(In7), .CLK(CLK), .Q(Out7));
  FlipFlopD flipflopd_9 (.Data(In8), .CLK(CLK), .Q(Out8));
  FlipFlopD flipflopd_10 (.Data(In9), .CLK(CLK), .Q(Out9));
  FlipFlopD flipflopd_11 (.Data(In10), .CLK(CLK), .Q(Out10));
endmodule
