// Logisim project circuito.circ as structural Verilog: 3 circuits, main circuit main
module main (
);

  Reg11bits reg11bits_1 ();  // open: CLK, In0, Out0, In1, Out1, In2, Out2, In3, Out3, In4, Out4, In5, Out5, In6, Out6, In7, Out7, In8, Out8, In9, Out9, In10, Out10, In11, Out11
endmodule

module FlipFlopD (
  input  Data,
  input  CLK,
  output Q
);

  wire and_1_out, and_2_out, nor_2_out, not_1_out;

  not not_1 (not_1_out, Data);
  and and_1 (and_1_out, not_1_out, CLK);
  and and_2 (and_2_out, CLK, Data);
  nor nor_1 (Q, and_1_out, nor_2_out);
  nor nor_2 (nor_2_out, Q, and_2_out);
endmodule

module Reg11bits (
  input  In0,
  input  In1,
  input  In2,
  input  In3,
  input  In4,
  input  In5,
  input  In6,
  input  In7,
  input  In8,
  input  In9,
  input  In10,
  input  In11,
  input  CLK,
  output Out0,
  output Out1,
  output Out2,
  output Out3,
  output Out4,
  output Out5,
  output Out6,
  output Out7,
  output Out8,
  output Out9,
  output Out10,
  output Out11
);

  FlipFlopD flipflopd_1 (.Data(In0), .CLK(CLK), .Q(Out0));
  FlipFlopD flipflopd_2 (.Data(In1), .CLK(CLK), .Q(Out1));
  FlipFlopD flipflopd_3 (.Data(In2), .CLK(CLK), .Q(Out2));
  FlipFlopD flipflopd_4 (.Data(In3), .CLK(CLK), .Q(Out3));
  FlipFlopD flipflopd_5 (.Data(In4), .CLK(CLK), .Q(Out4));
  FlipFlopD flipflopd_6 (.Data(In5), .CLK(CLK), .Q(Out5));
  FlipFlopD flipflopd_7 (.Data(In6), .CLK(CLK), .Q(Out6));
  FlipFlopD flipflopd_8 (.Data(In7), .CLK(CLK), .Q(Out7));
  FlipFlopD flipflopd_9 (.Data(In8), .CLK(CLK), .Q(Out8));
  FlipFlopD flipflopd_10 (.Data(In9), .CLK(CLK), .Q(Out9));
  FlipFlopD flipflopd_11 (.Data(In10), .CLK(CLK), .Q(Out10));
  FlipFlopD flipflopd_12 (.Data(In11), .CLK(CLK), .Q(Out11));
endmodule
