// Logisim project Aula25-02.circ as structural Verilog: 8 circuits, main circuit main
module main (
  input  a,
  input  b,
  input  c,
  input  in_4,
  input  in_5,
  input  in_6,
  input  in_7,
  input  in_8,
  input  in_9,
  input  in_10,
  input  in_11,
  input  in_12,
  output M,
  output out_14,
  output out_15,
  output out_16,
  output out_17,
  output out_18,
  output out_19,
  output out_20,
  output out_21
);

  wire and_1_out, and_2_out, and_3_out, and_4_out, not_1_out, not_2_out, not_3_out;

  not not_1 (not_1_out, a);
  not not_2 (not_2_out, b);
  not not_3 (not_3_out, c);
  and and_1 (and_1_out, not_1_out, b, c);
  and and_2 (and_2_out, a, not_2_out, c);
  and and_3 (and_3_out, a, b, not_3_out);
  and and_4 (and_4_out, a, b, c);
  Reg8bits reg8bits_1 (
    .CLK(in_4), .In0(in_5), .Out0(out_14), .In1(in_6), .Out1(out_15), .In2(in_7), .Out2(out_16), .In3(in_8),
    .Out3(out_17), .In4(in_9), .Out4(out_18), .In5(in_10), .Out5(out_19), .In6(in_11), .Out6(out_20),
    .In7(in_12), .Out7(out_21));
  or or_1 (M, and_1_out, and_2_out, and_3_out, and_4_out);
endmodule

module decoder2bits (
  input  A1,
  input  A2,
  input  E,
  output D0,
  output D02,
  output D03,
  output D04
);

  wire not_1_out, not_2_out, not_3_out, not_4_out;

  not not_1 (not_1_out, A1);
  not not_2 (not_2_out, A2);
  not not_3 (not_3_out, A1);
  not not_4 (not_4_out, A2);
  and and_1 (D04, E, A1, A2);
  and and_2 (D0, E, not_1_out, not_2_out);
  and and_3 (D02, E, not_3_out, A2);
  and and_4 (D03, E, A1, not_4_out);
endmodule

module decoder3bits (
  input  in_1,
  input  in_2,
  input  in_3,
  input  in_4,
  output out_5,
  output out_6,
  output out_7,
  output out_8,
  output out_9,
  output out_10,
  output out_11,
  output out_12
);

  wire not_1_out, not_2_out, not_3_out;

  not not_1 (not_1_out, in_1);
  not not_2 (not_2_out, in_2);
  not not_3 (not_3_out, in_3);
  buf and_1 (out_5, in_4);  // AND_Gate
  buf and_2 (out_6, in_4);  // AND_Gate
  buf and_3 (out_8, in_4);  // AND_Gate
  buf and_4 (out_7, in_4);  // AND_Gate
  buf and_5 (out_9, in_4);  // AND_Gate
  buf and_6 (out_10, in_4);  // AND_Gate
  buf and_7 (out_12, in_4);  // AND_Gate
  buf and_8 (out_11, in_4);  // AND_Gate
endmodule

module FlipFlopRS (
  input  R,
  input  S,
  output Q,
  output NotQ
);

  nor nor_1 (Q, R, NotQ);
  nor nor_2 (NotQ, Q, S);
endmodule

module FlipFlopNand (
  input  Set,
  input  Reset,
  output Q,
  output NotQ
);

  wire not_1_out, not_2_out;

  not not_1 (not_1_out, Set);
  not not_2 (not_2_out, Reset);
  nand nand_1 (Q, not_1_out, NotQ);
  nand nand_2 (NotQ, Q, not_2_out);
endmodule

module FlipFlopRSSincrono (
  input  R,
  input  C,
  input  S,
  output Q,
  output NQ
);

  wire and_1_out, and_2_out;

  and and_1 (and_1_out, R, C);
  and and_2 (and_2_out, C, S);
  nor nor_1 (Q, and_1_out, NQ);
  nor nor_2 (NQ, Q, and_2_out);
endmodule

module FlipFlopD (
  input  Data,
  input  CLK,
  output Q
);

  wire and_1_out, and_2_out, nor_2_out, not_1_out;

  not not_1 (not_1_out, Data);
  and and_1 (and_1_out, not_1_out, CLK);
  and and_2 (and_2_out, CLK, Data);
  nor nor_1 (Q, and_1_out, nor_2_out);
  nor nor_2 (nor_2_out, Q, and_2_out);
endmodule

module Reg8bits (
  input  In0,
  input  In1,
  input  In2,
  input  In3,
  input  CLK,
  input  In4,
  input  In5,
  input  In6,
  input  In7,
  output Out0,
  output Out1,
  output Out2,
  output Out3,
  output Out4,
  output Out5,
  output Out6,
  output Out7
);

  FlipFlopD flipflopd_1 (.Data(In0), .CLK(CLK), .Q(Out0));
  FlipFlopD flipflopd_2 (.Data(In4), .CLK(CLK), .Q(Out4));
  FlipFlopD flipflopd_3 (.Data(In1), .CLK(CLK), .Q(Out1));
  FlipFlopD flipflopd_4 (.Data(In5), .CLK(CLK), .Q(Out5));
  FlipFlopD flipflopd_5 (.Data(In2), .CLK(CLK), .Q(Out2));
  FlipFlopD flipflopd_6 (.Data(In6), .CLK(CLK), .Q(Out6));
  FlipFlopD flipflopd_7 (.Data(In3), .CLK(CLK), .Q(Out3));
  FlipFlopD flipflopd_8 (.Data(In7), .CLK(CLK), .Q(Out7));
endmodule
