// Logisim project Somador (1).circ as structural Verilog
module Somador1Bit (
  input  A,
  input  B,
  input  Carry_In,
  output Out,
  output Carry_Out
);

  wire and_1_out, and_2_out, and_3_out, xor_1_out;

  xor xor_1 (xor_1_out, A, B);
  and and_1 (and_1_out, A, B);
  and and_2 (and_2_out, A, Carry_In);
  and and_3 (and_3_out, B, Carry_In);
  xor xor_2 (Out, xor_1_out, Carry_In);
  or or_1 (Carry_Out, and_1_out, and_2_out, and_3_out);
endmodule

module Somador4Bits (
  input  Carry_In,
  input  B3,
  input  A3,
  input  B2,
  input  A2,
  input  B1,
  input  A1,
  input  B0,
  input  A0,
  output Carry_Out,
  output C3,
  output C2,
  output C1,
  output C0
);

  wire somador1bit_2_carry_out, somador1bit_3_carry_out, somador1bit_4_carry_out;

  Somador1Bit somador1bit_1 (.A(A3), .B(B3), .Carry_In(somador1bit_2_carry_out), .Out(C3), .Carry_Out(Carry_Out));
  Somador1Bit somador1bit_2 (
    .A(A2), .B(B2), .Carry_In(somador1bit_3_carry_out), .Out(C2), .Carry_Out(somador1bit_2_carry_out));
  Somador1Bit somador1bit_3 (
    .A(A1), .B(B1), .Carry_In(somador1bit_4_carry_out), .Out(C1), .Carry_Out(somador1bit_3_carry_out));
  Somador1Bit somador1bit_4 (.A(A0), .B(B0), .Carry_In(Carry_In), .Out(C0), .Carry_Out(somador1bit_4_carry_out));
endmodule

module Somador8Bits (
  input  B7,
  input  A7,
  input  B6,
  input  A6,
  input  B5,
  input  A5,
  input  B4,
  input  A4,
  input  B3,
  input  A3,
  input  B2,
  input  A2,
  input  B1,
  input  A1,
  input  B0,
  input  A0,
  input  Carry_In,
  output Carry_Out,
  output C7,
  output C6,
  output C5,
  output C4,
  output C3,
  output C2,
  output C1,
  output C0
);

  wire somador4bits_2_carry_out;

  Somador4Bits somador4bits_1 (
    .B3(B7), .A3(A7), .B2(B6), .A2(A6), .B1(B5), .A1(A5), .Carry_In(somador4bits_2_carry_out), .B0(B4),
    .A0(A4), .Carry_Out(Carry_Out), .C3(C7), .C2(C6), .C1(C5), .C0(C4));
  Somador4Bits somador4bits_2 (
    .B3(B3), .A3(A3), .B2(B2), .A2(A2), .B1(B1), .A1(A1), .Carry_In(Carry_In), .B0(B0), .A0(A0),
    .Carry_Out(somador4bits_2_carry_out), .C3(C3), .C2(C2), .C1(C1), .C0(C0));
endmodule
