// Logisim project Somador.circ as structural Verilog: 4 circuits, main circuit main
module main (
  input  A7,
  input  A6,
  input  A5,
  input  A4,
  input  A3,
  input  A2,
  input  A1,
  input  A0,
  input  B7,
  input  B6,
  input  B5,
  input  B4,
  input  B3,
  input  B2,
  input  B1,
  input  B0,
  output C0,
  output C1,
  output C2,
  output C3,
  output C4,
  output C5,
  output C6,
  output C7,
  output COUT
);

  Sum8Bits sum8bits_1 (
    .B7(B7), .A7(A7), .B6(B6), .A6(A6), .B5(B5), .A5(A5), .B4(B4), .A4(A4), .B3(B3), .A3(A3), .B2(B2),
    .A2(A2), .B1(B1), .A1(A1), .B0(B0), .A0(A0), .COut(COUT), .C7(C7), .C6(C6), .C5(C5), .C4(C4), .C3(C3),
    .C2(C2), .C1(C1), .C0(C0), .CIn(1'b0));
endmodule

module Sum1Bit (
  input  A,
  input  B,
  input  CIn,
  output Out,
  output COut
);

  wire and_1_out, and_2_out, and_3_out, xor_1_out;

  xor xor_1 (xor_1_out, A, B);
  and and_1 (and_1_out, A, B);
  and and_2 (and_2_out, A, CIn);
  and and_3 (and_3_out, B, CIn);
  xor xor_2 (Out, xor_1_out, CIn);
  or or_1 (COut, and_1_out, and_2_out, and_3_out);
endmodule

module Sum4Bits (
  input  CIn,
  input  B3,
  input  A3,
  input  B2,
  input  A2,
  input  B1,
  input  A1,
  input  B0,
  input  A0,
  output COut,
  output C3,
  output C2,
  output C1,
  output C0
);

  wire sum1bit_2_cout, sum1bit_3_cout, sum1bit_4_cout;

  Sum1Bit sum1bit_1 (.A(A3), .B(B3), .CIn(sum1bit_2_cout), .Out(C3), .COut(COut));
  Sum1Bit sum1bit_2 (.A(A2), .B(B2), .CIn(sum1bit_3_cout), .Out(C2), .COut(sum1bit_2_cout));
  Sum1Bit sum1bit_3 (.A(A1), .B(B1), .CIn(sum1bit_4_cout), .Out(C1), .COut(sum1bit_3_cout));
  Sum1Bit sum1bit_4 (.A(A0), .B(B0), .CIn(CIn), .Out(C0), .COut(sum1bit_4_cout));
endmodule

module Sum8Bits (
  input  B7,
  input  A7,
  input  B6,
  input  A6,
  input  B5,
  input  A5,
  input  B4,
  input  A4,
  input  B3,
  input  A3,
  input  B2,
  input  A2,
  input  B1,
  input  A1,
  input  B0,
  input  A0,
  input  CIn,
  output COut,
  output C7,
  output C6,
  output C5,
  output C4,
  output C3,
  output C2,
  output C1,
  output C0
);

  wire sum4bits_2_cout;

  Sum4Bits sum4bits_1 (
    .B3(B7), .A3(A7), .B2(B6), .A2(A6), .B1(B5), .A1(A5), .CIn(sum4bits_2_cout), .B0(B4), .A0(A4),
    .COut(COut), .C3(C7), .C2(C6), .C1(C5), .C0(C4));
  Sum4Bits sum4bits_2 (
    .B3(B3), .A3(A3), .B2(B2), .A2(A2), .B1(B1), .A1(A1), .CIn(CIn), .B0(B0), .A0(A0),
    .COut(sum4bits_2_cout), .C3(C3), .C2(C2), .C1(C1), .C0(C0));
endmodule
