// Logisim project SomadorEvolution.circ as structural Verilog: 5 circuits, main circuit main
module main (
);

  Somador32Bits somador32bits_1 ();  // open: C_In, b15, b7, b31, b23, a15, a7, a31, a23, b14, b6, b30, b22, a14, a6, a30, a22, b13, b5, b29, b21, a13, a5, a29, a21, b12, b4, b28, b20, a12, a4, a28, a20, b11, b3, b27, b19, a11, a3, a27, a19, b10, b2, b26, b18, a10, a2, a26, a18, b9, b1, b25, b17, a9, a1, a25, a17, b8, b0, b24, b16, a8, a0, a24, a16, c31, c15, c7, c30, c23, c14, c6, c29, c22, c13, c5, c28, c21, c12, c4, c27, c20, c11, c3, c26, c19, c10, c2, c25, c18, c9, c1, c24, c17, c8, c0, c16, C_Out
endmodule

module Somador1Bit (
  input  a0,
  input  b0,
  input  C_In,
  output S,
  output C_Out
);

  wire and_1_out, and_2_out, and_3_out, xor_1_out;

  and and_1 (and_1_out, a0, b0);
  and and_2 (and_2_out, a0, C_In);
  and and_3 (and_3_out, b0, C_In);
  xor xor_1 (xor_1_out, a0, b0);
  xor xor_2 (S, xor_1_out, C_In);
  or or_1 (C_Out, and_1_out, and_2_out, and_3_out);
endmodule

module Somador4Bits (
  input  C_In,
  input  b3,
  input  a3,
  input  b2,
  input  a2,
  input  b1,
  input  a1,
  input  b0,
  input  a0,
  output C_Out,
  output c3,
  output C2,
  output C1,
  output c0
);

  wire somador1bit_2_c_out, somador1bit_3_c_out, somador1bit_4_c_out;

  Somador1Bit somador1bit_1 (.a0(a3), .b0(b3), .C_In(somador1bit_2_c_out), .S(c3), .C_Out(C_Out));
  Somador1Bit somador1bit_2 (.a0(a2), .b0(b2), .C_In(somador1bit_3_c_out), .S(C2), .C_Out(somador1bit_2_c_out));
  Somador1Bit somador1bit_3 (.a0(a1), .b0(b1), .C_In(somador1bit_4_c_out), .S(C1), .C_Out(somador1bit_3_c_out));
  Somador1Bit somador1bit_4 (.a0(a0), .b0(b0), .C_In(C_In), .S(c0), .C_Out(somador1bit_4_c_out));
endmodule

module Somador8Bits (
  input  C_In,
  input  b7,
  input  a7,
  input  b6,
  input  a6,
  input  b5,
  input  a5,
  input  b4,
  input  a4,
  input  b3,
  input  a3,
  input  b2,
  input  a2,
  input  b1,
  input  a1,
  input  b0,
  input  a0,
  output C_Out,
  output c7,
  output c6,
  output c5,
  output c4,
  output c3,
  output c2,
  output c1,
  output c0
);

  wire somador4bits_2_c_out;

  Somador4Bits somador4bits_1 (
    .C_In(somador4bits_2_c_out), .b3(b7), .a3(a7), .b2(b6), .a2(a6), .b1(b5), .a1(a5), .b0(b4), .a0(a4),
    .C_Out(C_Out), .c3(c7), .C2(c6), .C1(c5), .c0(c4));
  Somador4Bits somador4bits_2 (
    .C_In(C_In), .b3(b3), .a3(a3), .b2(b2), .a2(a2), .b1(b1), .a1(a1), .b0(b0), .a0(a0),
    .C_Out(somador4bits_2_c_out), .c3(c3), .C2(c2), .C1(c1), .c0(c0));
endmodule

module Somador32Bits (
  input  C_In,
  input  b15,
  input  b7,
  input  b31,
  input  b23,
  input  a15,
  input  a7,
  input  a31,
  input  a23,
  input  b14,
  input  b6,
  input  b30,
  input  b22,
  input  a14,
  input  a6,
  input  a30,
  input  a22,
  input  b13,
  input  b5,
  input  b29,
  input  b21,
  input  a13,
  input  a5,
  input  a29,
  input  a21,
  input  b12,
  input  b4,
  input  b28,
  input  b20,
  input  a12,
  input  a4,
  input  a28,
  input  a20,
  input  b11,
  input  b3,
  input  b27,
  input  b19,
  input  a11,
  input  a3,
  input  a27,
  input  a19,
  input  b10,
  input  b2,
  input  b26,
  input  b18,
  input  a10,
  input  a2,
  input  a26,
  input  a18,
  input  b9,
  input  b1,
  input  b25,
  input  b17,
  input  a9,
  input  a1,
  input  a25,
  input  a17,
  input  b8,
  input  b0,
  input  b24,
  input  b16,
  input  a8,
  input  a0,
  input  a24,
  input  a16,
  output c31,
  output c15,
  output c7,
  output c30,
  output c23,
  output c14,
  output c6,
  output c29,
  output c22,
  output c13,
  output c5,
  output c28,
  output c21,
  output c12,
  output c4,
  output c27,
  output c20,
  output c11,
  output c3,
  output c26,
  output c19,
  output c10,
  output c2,
  output c25,
  output c18,
  output c9,
  output c1,
  output c24,
  output c17,
  output c8,
  output c0,
  output c16,
  output C_Out
);

  wire somador8bits_2_c_out, somador8bits_3_c_out, somador8bits_4_c_out;

  Somador8Bits somador8bits_1 (
    .C_In(somador8bits_2_c_out), .b7(b31), .a7(a31), .b6(b30), .a6(a30), .b5(b29), .a5(a29), .b4(b28),
    .a4(a28), .b3(b27), .a3(a27), .b2(b26), .a2(a26), .b1(b25), .a1(a25), .b0(b24), .a0(a24), .C_Out(c31),
    .c7(c30), .c6(c29), .c5(c28), .c4(c27), .c3(c26), .c2(c25), .c1(c24), .c0(C_Out));
  Somador8Bits somador8bits_2 (
    .C_In(somador8bits_3_c_out), .b7(b23), .a7(a23), .b6(b22), .a6(a22), .b5(b21), .a5(a21), .b4(b20),
    .a4(a20), .b3(b19), .a3(a19), .b2(b18), .a2(a18), .b1(b17), .a1(a17), .b0(b16), .a0(a16),
    .C_Out(somador8bits_2_c_out), .c7(c23), .c6(c22), .c5(c21), .c4(c20), .c3(c19), .c2(c18), .c1(c17),
    .c0(c16));
  Somador8Bits somador8bits_3 (
    .C_In(somador8bits_4_c_out), .b7(b15), .a7(a15), .b6(b14), .a6(a14), .b5(b13), .a5(a13), .b4(b12),
    .a4(a12), .b3(b11), .a3(a11), .b2(b10), .a2(a10), .b1(b9), .a1(a9), .b0(b8), .a0(a8),
    .C_Out(somador8bits_3_c_out), .c7(c15), .c6(c14), .c5(c13), .c4(c12), .c3(c11), .c2(c10), .c1(c9), .c0(c8));
  Somador8Bits somador8bits_4 (
    .C_In(C_In), .b7(b7), .a7(a7), .b6(b6), .a6(a6), .b5(b5), .a5(a5), .b4(b4), .a4(a4), .b3(b3), .a3(a3),
    .b2(b2), .a2(a2), .b1(b1), .a1(a1), .b0(b0), .a0(a0), .C_Out(somador8bits_4_c_out), .c7(c7), .c6(c6),
    .c5(c5), .c4(c4), .c3(c3), .c2(c2), .c1(c1), .c0(c0));
endmodule
