// Logisim project SomadorTeste.circ as structural Verilog
module Seletor1bit (
  input  S,
  input  a0,
  input  a1
);

  wire and_1_out, and_2_out, not_1_out, or_1_out;

  not not_1 (not_1_out, S);
  and and_1 (and_1_out, not_1_out, a0);
  and and_2 (and_2_out, S, a1);
  or or_1 (or_1_out, and_1_out, and_2_out);
  // Probe on or_1_out
endmodule

module Somador1bit (
  input  a0,
  input  a1,
  input  C_In,
  output S,
  output C_Out
);

  wire and_1_out, and_2_out, and_3_out, xor_1_out;

  and and_1 (and_1_out, a0, a1);
  and and_2 (and_2_out, a0, C_In);
  and and_3 (and_3_out, a1, C_In);
  xor xor_1 (xor_1_out, a0, a1);
  xor xor_2 (S, xor_1_out, C_In);
  or or_1 (C_Out, and_1_out, and_2_out, and_3_out);
endmodule

module Somador4bit (
  input  b3,
  input  a3,
  input  b2,
  input  a2,
  input  b1,
  input  a1,
  input  b0,
  input  a0,
  output C_Out,
  output c3,
  output c2,
  output c1,
  output c0
);

  wire somador1bit_2_c_out, somador1bit_3_c_out, somador1bit_4_c_out;

  Somador1bit somador1bit_1 (.a0(a3), .a1(b3), .C_In(somador1bit_2_c_out), .S(c3), .C_Out(C_Out));
  Somador1bit somador1bit_2 (.a0(a2), .a1(b2), .C_In(somador1bit_3_c_out), .S(c2), .C_Out(somador1bit_2_c_out));
  Somador1bit somador1bit_3 (.a0(a1), .a1(b1), .C_In(somador1bit_4_c_out), .S(c1), .C_Out(somador1bit_3_c_out));
  Somador1bit somador1bit_4 (.a0(a0), .a1(b0), .C_In(1'b0), .S(c0), .C_Out(somador1bit_4_c_out));
endmodule

module Somador8bit (
  input  in_1
);

  wire somador4bit_2_c0, somador4bit_2_c1, somador4bit_2_c_out;

  Somador4bit somador4bit_1 ();  // open: C_Out, b3, a3, b2, a2, b1, a1, b0, a0, c3, c2, c1, c0
  Somador4bit somador4bit_2 (
    .C_Out(somador4bit_2_c_out), .c1(somador4bit_2_c1), .c0(somador4bit_2_c0));  // open: b3, a3, b2, a2, b1, a1, b0, a0, c3, c2
endmodule
